// Logisim project BigASM.circ as structural Verilog
module BOARD_BIG_ASM (
  output out_1
);

  wire button_1_out, button_2_out, CLK, CLR, d_ff_1_q, not_1_out, Write, Write_ASCII;
  wire [6:0] ASCII;
  wire [7:0] counter_1_q;
  wire [23:0] Dir_INPUT, Dir_MEMORY;
  wire [31:0] INPUT, MEMORY_IN, MEMORY_OUT;

  Button button_1 (.out(button_1_out));
  Button button_2 (.out(button_2_out));
  Clock clock_1 (.out(CLK));
  D_Flip_Flop d_ff_1 (.clk(CLK), .D(1'b1), .Q(d_ff_1_q), .reset(button_1_out));  // open: Qn, preset, en
  // Probe on INPUT
  D_Flip_Flop d_ff_2 (.clk(CLK), .D(d_ff_1_q), .Qn(CLR), .reset(button_1_out));  // open: Q, preset, en
  BIG_ASM big_asm_1 (
    .MEMORY_IN(MEMORY_OUT), .CLK(CLK), .CLR(CLR), .DIR_INPUT(Dir_INPUT), .MEMORY_OUT(MEMORY_IN),
    .DIR_MEMORY(Dir_MEMORY), .Write_OUTPUT(Write), .ASCII(ASCII), .Write_ASCII(Write_ASCII), .END(out_1),
    .DATA_INPUT(INPUT), .start(button_2_out));
  MEMORY memory_1 (.DIR(Dir_MEMORY), .DATA_IN(MEMORY_IN), .WRITE(Write), .CLK(CLK), .CLR(CLR), .DATA_OUT(MEMORY_OUT));
  INPUT input_1 (.DIR(Dir_INPUT), .CLK(CLK), .DATA_OUT(INPUT));
  Counter counter_1 (.load(1'b0), .count(not_1_out), .Q(counter_1_q), .clk(CLK), .clr(CLR));  // open: D, carry
  not not_1 (not_1_out, out_1);
  // Probe on counter_1_q
  TTY #(.rows(32), .cols(60)) tty_1 (.data(ASCII), .clk(CLK), .we(Write_ASCII), .clr(CLR));

  // Other names for the same wires on the sheet: END = out_1

  // Notes on the sheet:
  //   COUNTER
  //   BOARD
endmodule

module INPUT (
  input  [23:0] DIR,
  input  CLK,
  output [31:0] DATA_OUT
);

  RAM #(.addrWidth(24), .dataWidth(32)) ram_1 (.addr(DIR), .data(DATA_OUT), .clk(CLK), .ld(1'b1));  // open: sel, clr
endmodule

module MEMORY (
  input  [23:0] DIR,
  input  [31:0] DATA_IN,
  input  WRITE,
  input  CLK,
  input  CLR,
  output [31:0] DATA_OUT
);

  wire not_1_out;

  not not_1 (not_1_out, WRITE);
  RAM #(.addrWidth(24), .dataWidth(32), .bus("separate")) ram_1 (
    .addr(DIR), .din(DATA_IN), .data(DATA_OUT), .clk(CLK), .ld(not_1_out), .clr(CLR));  // open: str, sel
endmodule

module BIG_ASM (
  input  [31:0] DATA_INPUT,
  input  [31:0] MEMORY_IN,
  input  CLK,
  input  CLR,
  input  start,
  output [23:0] DIR_INPUT,
  output [31:0] MEMORY_OUT,
  output [23:0] DIR_MEMORY,
  output Write_OUTPUT,
  output [6:0] ASCII,
  output Write_ASCII,
  output END
);

  wire i____n, Li0, Li0_2, Li1, Li1_2, Lm, Ln, Ln_2, Ls0, Ls0_2, Ls1, Ls1_2, Ls2, Ls2_2, Lw, Lw_2,
       media_dp_1_i____n, Media_End, print_dec_1_end, Si, Si_2, Ss0, Ss0_2, Ss1, Ss1_2, Sw, Sw_2,
       varianza_cu_1_start_print;
  wire [23:0] adress_V, media_dp_1_adress;
  wire [31:0] Media, varianza_dp_1_output;

  Media_DP media_dp_1 (
    .END(Media_End), .Adress(media_dp_1_adress), .CLk(CLK), .Input(DATA_INPUT), .Output(Media), .Ln(Ln),
    .Ls0(Ls0), .Ls1(Ls1), .Ls2(Ls2), .Li0(Li0), .Li1(Li1), .Lw(Lw), .Sw(Sw), .Si(Si), .Ss0(Ss0), .Ss1(Ss1),
    .CLR(CLR), .i____n(media_dp_1_i____n));
  Varianza_DP varianza_dp_1 (
    .END(varianza_cu_1_start_print), .Adress(adress_V), .CLk(CLK), .Input(DATA_INPUT),
    .Output(varianza_dp_1_output), .Ln(Ln_2), .Ls0(Ls0_2), .Ls1(Ls1_2), .Ls2(Ls2_2), .Li0(Li0_2),
    .Li1(Li1_2), .Lw(Lw_2), .Sw(Sw_2), .Si(Si_2), .Ss0(Ss0_2), .Ss1(Ss1_2), .Lm(Lm), .media(Media),
    .CLR(CLR), .i____n(i____n));
  Media_CU media_cu_1 (
    .CLK(CLK), .Start(start), .Ln(Ln), .Ls0(Ls0), .Li0(Li0), .Li1(Li1), .Ls1(Ls1), .Ss0(Ss0), .Si(Si),
    .i____n(media_dp_1_i____n), .Ss1(Ss1), .Ls2(Ls2), .Sw(Sw), .Lw(Lw), .CLR(CLR), .END(Media_End));
  Varianza_CU varianza_cu_1 (
    .CLK(CLK), .Start(start), .Ln(Ln_2), .Ls0(Ls0_2), .Li0(Li0_2), .Li1(Li1_2), .Ls1(Ls1_2), .Ss0(Ss0_2),
    .Si(Si_2), .i____n(i____n), .Ss1(Ss1_2), .Ls2(Ls2_2), .Sw(Sw_2), .Lw(Lw_2), .Lm(Lm),
    .Media_End(Media_End), .CLR(CLR), .Start_Print(varianza_cu_1_start_print), .Print_End(print_dec_1_end),
    .END(END));
  PRINT_DEC print_dec_1 (
    .num(varianza_dp_1_output), .start(varianza_cu_1_start_print), .CLK(CLK), .RST(CLR), .ASCII(ASCII),
    .Write_ASCII(Write_ASCII), .END(print_dec_1_end));
  Multiplexer #(.width(24), .enable("false")) multiplexer_1 (
    .in0(media_dp_1_adress), .in1(adress_V), .out(DIR_INPUT), .sel(Media_End));

  // Other names for the same wires on the sheet: clear = CLR; clock = CLK
endmodule

module PRINT_UDEC (
  input  [31:0] num,
  input  start,
  input  CLK,
  input  RST,
  output [6:0] ASCII,
  output Write_ASCII,
  output \end 
);

  wire _0_c, _0_n, demultiplexer_1_out0, demultiplexer_2_out0, demultiplexer_2_out1, demultiplexer_3_out0,
       demultiplexer_3_out1, IDLE_2_q, IDLE_3_q, IDLE_4_q, IDLE_q, Lc, Lc_0, Ln, Ln_0, or_1_out;
  wire [23:0] bit_extender_1_out;
  wire [31:0] c, c___1, c___1_t, divider_1_rem, memory_1_data_out, multiplexer_1_out, multiplexer_2_out,
       multiplexer_3_out, n, n___10, n___10___48;

  Multiplexer #(.width(32), .enable("false")) multiplexer_1 (
    .in0(num), .in1(n___10), .out(multiplexer_1_out), .sel(Lc_0));
  Divider #(.width(32)) divider_1 (.a(n), .b(32'ha), .out(n___10), .rem(divider_1_rem));  // open: upper
  Adder #(.width(32)) adder_1 (.a(divider_1_rem), .b(32'h30), .out(n___10___48));  // open: cin, cout
  or or_1 (or_1_out, demultiplexer_1_out0, \end );
  Register #(.width(32)) u_n (.D(multiplexer_1_out), .en(Ln), .Q(n), .clk(CLK), .clr(RST));
  D_Flip_Flop IDLE (.clk(CLK), .D(or_1_out), .Q(IDLE_q), .preset(RST));  // open: Qn, en, reset
  Demultiplexer #(.enable("false")) demultiplexer_1 (
    .out0(demultiplexer_1_out0), .out1(Ln_0), .in(IDLE_q), .sel(start));
  or or_2 (Write_ASCII, demultiplexer_3_out0, demultiplexer_2_out1);
  Multiplexer #(.width(32), .enable("false")) multiplexer_2 (
    .in0(c___1), .in1(c___1_t), .out(multiplexer_2_out), .sel(Write_ASCII));
  Adder #(.width(32)) adder_2 (.a(c), .b(32'h1), .out(c___1));  // open: cin, cout
  Subtractor #(.width(32)) subtractor_1 (.a(c), .b(32'h1), .out(c___1_t));  // open: bin, bout
  D_Flip_Flop IDLE_2 (.clk(CLK), .D(Ln_0), .Q(IDLE_2_q), .reset(RST));  // open: Qn, preset, en
  Register #(.width(32)) u_c (.D(multiplexer_2_out), .en(Lc), .Q(c), .clk(CLK), .clr(RST));
  or or_3 (Lc_0, IDLE_2_q, demultiplexer_3_out1);
  Multiplexer #(.width(32), .enable("false")) multiplexer_3 (
    .in0(c), .in1(c___1_t), .out(multiplexer_3_out), .sel(Write_ASCII));
  Comparator #(.width(32), .mode("unsigned")) comparator_1 (.a({32{1'b0}}), .b(n), .lt(_0_n));  // open: gt, eq
  Comparator #(.width(32), .mode("unsigned")) comparator_2 (.a({32{1'b0}}), .b(c), .lt(_0_c));  // open: gt, eq
  D_Flip_Flop IDLE_3 (.clk(CLK), .D(Write_ASCII), .Q(IDLE_3_q), .reset(RST));  // open: Qn, preset, en
  Demultiplexer #(.enable("false")) demultiplexer_2 (
    .out0(demultiplexer_2_out0), .out1(demultiplexer_2_out1), .in(IDLE_3_q), .sel(_0_c));
  Bit_Extender #(.in_width(32), .out_width(24)) bit_extender_1 (.in(multiplexer_3_out), .out(bit_extender_1_out));
  D_Flip_Flop IDLE_4 (.clk(CLK), .D(Lc_0), .Q(IDLE_4_q), .reset(RST));  // open: Qn, preset, en
  or or_4 (Lc, Lc_0, Write_ASCII);
  or or_5 (Ln, Ln_0, Lc_0);
  Demultiplexer #(.enable("false")) demultiplexer_3 (
    .out0(demultiplexer_3_out0), .out1(demultiplexer_3_out1), .in(IDLE_4_q), .sel(_0_n));
  D_Flip_Flop IDLE_5 (.clk(CLK), .D(demultiplexer_2_out0), .Q(\end ), .reset(RST));  // open: Qn, preset, en
  MEMORY memory_1 (
    .DIR(bit_extender_1_out), .DATA_IN(n___10___48), .WRITE(Lc_0), .CLK(CLK), .CLR(RST),
    .DATA_OUT(memory_1_data_out));
  Bit_Extender #(.in_width(32), .out_width(7)) bit_extender_2 (.in(memory_1_data_out), .out(ASCII));

  // Other names for the same wires on the sheet: Lc_1 = Write_ASCII; Sc = Write_ASCII; Ln_1 = Lc_0; Sn = Lc_0;
  //   Write = Lc_0
endmodule

module PRINT_DEC (
  input  [31:0] num,
  input  start,
  input  CLK,
  input  RST,
  output [6:0] ASCII,
  output Write_ASCII,
  output END
);

  wire demultiplexer_1_out0, demultiplexer_1_out1, demultiplexer_2_out0, demultiplexer_3_out0, end_t,
       IDLE_3_q, IDLE_q, or_1_out, or_2_out, or_3_out, S_ASCII, startUDEC, Write_ASCII_1;
  wire [6:0] ASCII_t;
  wire [31:0] multiplexer_1_out, negator_1_out;

  or or_1 (or_1_out, demultiplexer_1_out0, END);
  Negator #(.width(32)) negator_1 (.in(num), .out(negator_1_out));
  D_Flip_Flop IDLE (.clk(CLK), .D(or_1_out), .Q(IDLE_q), .preset(RST));  // open: Qn, en, reset
  Demultiplexer #(.enable("false")) demultiplexer_1 (
    .out0(demultiplexer_1_out0), .out1(demultiplexer_1_out1), .in(IDLE_q), .sel(start));
  Multiplexer #(.width(32), .enable("false")) multiplexer_1 (
    .in0(num), .in1(negator_1_out), .out(multiplexer_1_out), .sel(num[31]));
  Demultiplexer #(.enable("false")) demultiplexer_2 (
    .out0(demultiplexer_2_out0), .out1(S_ASCII), .in(demultiplexer_1_out1), .sel(num[31]));
  or or_2 (or_2_out, demultiplexer_2_out0, S_ASCII);
  D_Flip_Flop IDLE_2 (.clk(CLK), .D(or_2_out), .Q(startUDEC), .reset(RST));  // open: Qn, preset, en
  PRINT_UDEC print_udec_1 (
    .num(multiplexer_1_out), .start(startUDEC), .CLK(CLK), .RST(RST), .ASCII(ASCII_t),
    .Write_ASCII(Write_ASCII_1), .\end (end_t));
  D_Flip_Flop IDLE_3 (.clk(CLK), .D(or_3_out), .Q(IDLE_3_q), .reset(RST));  // open: Qn, preset, en
  or or_3 (or_3_out, startUDEC, demultiplexer_3_out0);
  Demultiplexer #(.enable("false")) demultiplexer_3 (
    .out0(demultiplexer_3_out0), .out1(END), .in(IDLE_3_q), .sel(end_t));
  Multiplexer #(.width(7), .enable("false")) multiplexer_2 (
    .in0(ASCII_t), .in1(7'b0101101), .out(ASCII), .sel(S_ASCII));
  or or_4 (Write_ASCII, S_ASCII, Write_ASCII_1);

  // Other names for the same wires on the sheet: sign = num[31]; Write_ASCII_0 = S_ASCII
endmodule

module TEST_PRINT (
  input  [31:0] in_1,
  output out_2
);

  wire button_1_out, button_2_out, CLK, CLR, d_ff_1_q, Write_ASCII;
  wire [6:0] ASCII;

  Button button_1 (.out(button_1_out));
  Clock clock_1 (.out(CLK));
  D_Flip_Flop d_ff_1 (.clk(CLK), .D(1'b1), .Q(d_ff_1_q), .reset(button_1_out));  // open: Qn, preset, en
  D_Flip_Flop d_ff_2 (.clk(CLK), .D(d_ff_1_q), .Qn(CLR), .reset(button_1_out));  // open: Q, preset, en
  Button button_2 (.out(button_2_out));
  PRINT_UDEC print_udec_1 ();  // open: num, start, CLK, RST, ASCII, Write_ASCII, end
  PRINT_DEC print_dec_1 (
    .num(in_1), .start(button_2_out), .CLK(CLK), .RST(CLR), .ASCII(ASCII), .Write_ASCII(Write_ASCII),
    .END(out_2));
  TTY #(.rows(32), .cols(60)) tty_1 (.data(ASCII), .clk(CLK), .we(Write_ASCII), .clr(CLR));
endmodule

module Cubo_DP (
  input  [31:0] Input,
  input  CLk,
  input  CLR,
  input  Lx0,
  input  Lx1,
  input  Sx,
  output [23:0] Addres,
  output [31:0] Output
);

  wire or_1_out;
  wire [31:0] A_A, multiplexer_1_out, X_A;

  Multiplier #(.width(32)) multiplier_1 (.a(Input), .b(Input), .out(A_A));  // open: cin, cout
  Multiplier #(.width(32)) multiplier_2 (.a(Output), .b(Input), .out(X_A));  // open: cin, cout
  Multiplexer #(.width(32), .enable("false")) multiplexer_1 (.in0(A_A), .in1(X_A), .out(multiplexer_1_out), .sel(Sx));
  Register #(.width(32)) register_1 (.D(multiplexer_1_out), .en(or_1_out), .Q(Output), .clk(CLk), .clr(CLR));
  or or_1 (or_1_out, Lx0, Lx1);

  assign Addres = {24{1'b0}};

  // Other names for the same wires on the sheet: A[31:0] = Input; Clear = CLR; clock = CLk; X[31:0] = Output
endmodule

module Cubo_CU (
  input  Start,
  input  CLR,
  input  Print_End,
  input  CLK,
  output END,
  output Start_Print,
  output Lx0,
  output Sx,
  output Lx1
);

  wire demultiplexer_1_out0, demultiplexer_2_out0, demultiplexer_2_out1, demultiplexer_3_out0,
       demultiplexer_3_out1, IDLE_q, or_1_out, or_2_out, or_3_out, Print_q;

  or or_1 (or_1_out, demultiplexer_1_out0, demultiplexer_2_out1);
  D_Flip_Flop IDLE (.clk(CLK), .D(or_1_out), .Q(IDLE_q), .preset(Start));  // open: Qn, en, reset
  Demultiplexer #(.enable("false")) demultiplexer_1 (.out0(demultiplexer_1_out0), .out1(Lx0), .in(IDLE_q), .sel(Start));
  D_Flip_Flop WAIT (.clk(CLK), .D(Lx0), .Q(Lx1), .reset(CLR));  // open: Qn, preset, en
  D_Flip_Flop u_END (.clk(CLK), .D(or_2_out), .Q(END), .reset(CLR));  // open: Qn, preset, en
  or or_2 (or_2_out, demultiplexer_2_out0, demultiplexer_3_out1);
  or or_3 (or_3_out, demultiplexer_3_out0, Lx1);
  Demultiplexer #(.enable("false")) demultiplexer_2 (
    .out0(demultiplexer_2_out0), .out1(demultiplexer_2_out1), .in(END), .sel(Start));
  Demultiplexer #(.enable("false")) demultiplexer_3 (
    .out0(demultiplexer_3_out0), .out1(demultiplexer_3_out1), .in(Print_q), .sel(Print_End));
  D_Flip_Flop Print (.clk(CLK), .D(or_3_out), .Q(Print_q), .reset(CLR));  // open: Qn, preset, en

  assign Start_Print = Lx1;
  assign Sx = Lx1;

  // Other names for the same wires on the sheet: Clear = CLR; clock = CLK
endmodule

module Paralelas_DP (
  input  CLk,
  input  L0,
  input  L1,
  input  L2,
  input  L3,
  input  L4,
  input  L5,
  input  L6,
  input  L7,
  input  Lw,
  input  Sw,
  input  CLk_2,
  input  [31:0] Input,
  input  END,
  output P,
  output [23:0] Adress,
  output [6:0] Output
);

  wire m1_positiva, m2_positiva, Pd, Pr, resta1_negativa, resta2_negativa, resta3_negativa, resta4_negativa;
  wire [23:0] multiplexer_6_out, w___1;
  wire [31:0] m1, m1_0, m1_0_A2, m1_1, m2, m2_0, m2_0_A2, m2_1, r1, r2, r3, r4, resta1, resta1_A2, resta2,
       resta2_A2, resta3, resta3_A2, resta4, resta4_A2, X1, X2, X3, X4, Y1, Y2, Y3, Y4;

  Register #(.width(32)) u_X1 (.D(Input), .en(L0), .Q(X1), .clk(CLk_2), .clr(CLk));
  // Probe on m1_0
  Divider #(.width(32)) divider_1 (.a(r1), .b(r2), .out(m1_0), .rem(m1_1));  // open: upper
  // Probe on m1_1
  Multiplexer #(.width(32), .enable("false")) multiplexer_1 (.in0(m1_0_A2), .in1(m1_0), .out(m1), .sel(m1_positiva));
  Complemento_A2 complemento_a2_1 (.Num(m1_0), .Num_A2(m1_0_A2));
  Subtractor #(.width(32)) subtractor_1 (.a(Y1), .b(Y2), .out(resta1));  // open: bin, bout
  Subtractor #(.width(32)) subtractor_2 (.a(X1), .b(X2), .out(resta2));  // open: bin, bout
  // Probe on resta1
  // Probe on resta2
  Register #(.width(32)) u_Y1 (.D(Input), .en(L1), .Q(Y1), .clk(CLk_2), .clr(CLk));
  Divider #(.width(32)) divider_2 (.a(r3), .b(r4), .out(m2_0), .rem(m2_1));  // open: upper
  Multiplexer #(.width(32), .enable("false")) multiplexer_2 (.in0(m2_0_A2), .in1(m2_0), .out(m2), .sel(m2_positiva));
  Complemento_A2 complemento_a2_2 (.Num(m2_0), .Num_A2(m2_0_A2));
  and and_1 (resta1_negativa, resta1[31], 1'b1);
  and and_2 (resta2_negativa, resta2[31], 1'b1);
  // Probe on m2_0
  // Probe on m2_1
  Comparator #(.width(32)) comparator_1 (.a(m1), .b(m2), .eq(Pd));  // open: gt, lt
  Register #(.width(32)) u_X2 (.D(Input), .en(L2), .Q(X2), .clk(CLk_2), .clr(CLk));
  Register #(.width(32)) u_Y2 (.D(Input), .en(L3), .Q(Y2), .clk(CLk_2), .clr(CLk));
  // Probe on r1
  Multiplexer #(.width(32), .enable("false")) multiplexer_3 (
    .in0(resta1), .in1(resta1_A2), .out(r1), .sel(resta1_negativa));
  Register #(.width(32)) u_X3 (.D(Input), .en(L4), .Q(X3), .clk(CLk_2), .clr(CLk));
  Comparator #(.width(32)) comparator_2 (.a(m1_1), .b(m2_1), .eq(Pr));  // open: gt, lt
  and and_3 (P, Pd, Pr);
  Multiplexer #(.width(7)) multiplexer_4 (.in0(7'b1000110), .in1(7'b1010100), .out(Output), .sel(P), .en(END));
  // Probe on r2
  Multiplexer #(.width(32), .enable("false")) multiplexer_5 (
    .in0(resta2), .in1(resta2_A2), .out(r2), .sel(resta2_negativa));
  Register #(.width(32)) u_Y3 (.D(Input), .en(L5), .Q(Y3), .clk(CLk_2), .clr(CLk));
  Complemento_A2 complemento_a2_3 (.Num(resta1), .Num_A2(resta1_A2));
  Complemento_A2 complemento_a2_4 (.Num(resta2), .Num_A2(resta2_A2));
  Register #(.width(32)) u_X4 (.D(Input), .en(L6), .Q(X4), .clk(CLk_2), .clr(CLk));
  Multiplexer #(.width(24), .enable("false")) multiplexer_6 (
    .in0({24{1'b0}}), .in1(w___1), .out(multiplexer_6_out), .sel(Sw));
  Adder #(.width(24)) adder_1 (.a(Adress), .b(24'h1), .out(w___1));  // open: cin, cout
  Register #(.width(32)) u_Y4 (.D(Input), .en(L7), .Q(Y4), .clk(CLk_2), .clr(CLk));
  xnor xnor_1 (m1_positiva, resta1_negativa, resta2_negativa);
  Register #(.width(24)) u_Adress (.D(multiplexer_6_out), .en(Lw), .Q(Adress), .clk(CLk_2), .clr(CLk));
  Multiplexer #(.width(32), .enable("false")) multiplexer_7 (
    .in0(resta3), .in1(resta3_A2), .out(r3), .sel(resta3_negativa));
  // Probe on resta1_A2
  // Probe on resta2_A2
  // Probe on r3
  Subtractor #(.width(32)) subtractor_3 (.a(Y3), .b(Y4), .out(resta3));  // open: bin, bout
  // Probe on resta3
  Subtractor #(.width(32)) subtractor_4 (.a(X3), .b(X4), .out(resta4));  // open: bin, bout
  // Probe on resta4
  and and_4 (resta4_negativa, resta4[31], 1'b1);
  // Probe on r4
  Multiplexer #(.width(32), .enable("false")) multiplexer_8 (
    .in0(resta4), .in1(resta4_A2), .out(r4), .sel(resta4_negativa));
  and and_5 (resta3_negativa, resta3[31], 1'b1);
  Complemento_A2 complemento_a2_5 (.Num(resta3), .Num_A2(resta3_A2));
  Complemento_A2 complemento_a2_6 (.Num(resta4), .Num_A2(resta4_A2));
  xnor xnor_2 (m2_positiva, resta3_negativa, resta4_negativa);
  // Probe on resta3_A2
  // Probe on resta4_A2

  // Other names for the same wires on the sheet: Clear = CLk; clock = CLk_2; w[23:0] = Adress; w0[31:0] = Input
endmodule

module Paralelas_CU (
  input  Start,
  input  CLR,
  input  Print_End,
  input  P,
  input  CLK,
  output END,
  output Lw,
  output L0,
  output L1,
  output L2,
  output L3,
  output L4,
  output L5,
  output L6,
  output L7,
  output Sw,
  output Start_Print
);

  wire demultiplexer_1_out0, demultiplexer_2_out0, demultiplexer_2_out1, demultiplexer_3_out0,
       demultiplexer_3_out1, demultiplexer_4_out0, demultiplexer_4_out1, END_qn, IDLE_q, or_1_out, or_5_out,
       or_6_out, Print_q, T_q, WAIT_8_q, WAIT_8_qn;

  or or_1 (or_1_out, demultiplexer_1_out0, demultiplexer_3_out1);
  D_Flip_Flop IDLE (.clk(CLK), .D(or_1_out), .Q(IDLE_q), .preset(Start));  // open: Qn, en, reset
  Demultiplexer #(.enable("false")) demultiplexer_1 (.out0(demultiplexer_1_out0), .out1(L0), .in(IDLE_q), .sel(Start));
  or or_2 (Lw, L0, L1, L2, L3, L4, L5, L6, L7);
  D_Flip_Flop WAIT (.clk(CLK), .D(L0), .Q(L1), .reset(CLR));  // open: Qn, preset, en
  D_Flip_Flop WAIT_2 (.clk(CLK), .D(L1), .Q(L2), .reset(CLR));  // open: Qn, preset, en
  D_Flip_Flop WAIT_3 (.clk(CLK), .D(L2), .Q(L3), .reset(CLR));  // open: Qn, preset, en
  D_Flip_Flop WAIT_4 (.clk(CLK), .D(L3), .Q(L4), .reset(CLR));  // open: Qn, preset, en
  or or_3 (Sw, L1, L2, L3, L4, L5, L6, L7);
  D_Flip_Flop WAIT_5 (.clk(CLK), .D(L4), .Q(L5), .reset(CLR));  // open: Qn, preset, en
  Demultiplexer #(.enable("false")) demultiplexer_2 (
    .out0(demultiplexer_2_out0), .out1(demultiplexer_2_out1), .in(WAIT_8_q), .sel(P));
  D_Flip_Flop WAIT_6 (.clk(CLK), .D(L5), .Q(L6), .reset(CLR));  // open: Qn, preset, en
  D_Flip_Flop WAIT_7 (.clk(CLK), .D(L6), .Q(L7), .reset(CLR));  // open: Qn, preset, en
  D_Flip_Flop T (.clk(CLK), .D(demultiplexer_2_out1), .Q(T_q), .reset(CLR));  // open: Qn, preset, en
  or or_4 (Start_Print, demultiplexer_2_out0, T_q);
  or or_5 (or_5_out, demultiplexer_3_out0, demultiplexer_4_out1);
  or or_6 (or_6_out, demultiplexer_4_out0, Start_Print);
  D_Flip_Flop WAIT_8 (.clk(CLK), .D(L7), .Q(WAIT_8_q), .Qn(WAIT_8_qn), .reset(CLR));  // open: preset, en
  D_Flip_Flop u_END (.clk(CLK), .D(or_5_out), .Q(END), .Qn(END_qn), .reset(CLR));  // open: preset, en
  D_Flip_Flop Print (.clk(CLK), .D(or_6_out), .Q(Print_q), .reset(CLR));  // open: Qn, preset, en
  Demultiplexer #(.enable("false")) demultiplexer_3 (
    .out0(demultiplexer_3_out0), .out1(demultiplexer_3_out1), .in(END), .sel(Start));
  Demultiplexer #(.enable("false")) demultiplexer_4 (
    .out0(demultiplexer_4_out0), .out1(demultiplexer_4_out1), .in(Print_q), .sel(Print_End));

  // Other names for the same wires on the sheet: Clear = CLR; clock = CLK; Lw0 = L0; Lw1 = L1; Sw1 = L1; Lw2 = L2;
  //   Sw2 = L2; Lw3 = L3; Sw3 = L3; Lw4 = L4; Sw4 = L4; Lw5 = L5; Sw5 = L5; Lw6 = L6; Sw6 = L6; Lw7 = L7; Sw7 = L7
endmodule

module Rectangulo_DP (
  input  L2,
  input  L3,
  input  L4,
  input  L5,
  input  L6,
  input  Clear,
  input  L0,
  input  L1,
  input  Lw,
  input  Sw,
  input  CLk,
  input  [31:0] Input,
  input  END,
  output [23:0] Adress,
  output C,
  output [6:0] Output
);

  wire C1, C2, C3, H1, H2, H3, m1_positiva, m2_positiva, m3_positiva, not_1_out, not_2_out, not_3_out,
       or_2_out, or_3_out, resta1_negativa, resta2_negativa, resta3_negativa, resta4_negativa,
       resta5_negativa, resta6_negativa, T1, T2, T3, V1, V2, V3, V_H;
  wire [23:0] multiplexer_7_out, w___1;
  wire [31:0] m1, m1_0, m1_0_A2, m1_1, m2, m2_0, m2_0_A2, m2_1, m3, m3_0, m3_0_A2, m3_1, multiplier_1_out,
       multiplier_2_out, multiplier_3_out, r1, r1_0, r2, r2_0, r3, r3_0, r4, r5, r6, resta1, resta1_A2,
       resta2, resta2_A2, resta3, resta3_A2, resta4, resta4_A2, resta5, resta5_A2, resta6, resta6_A2, X1, X2,
       X3, Y1, Y2, Y3;

  Divider #(.width(32)) divider_1 (.a(r1), .b(r2), .out(m1_0), .rem(m1_1));  // open: upper
  Multiplexer #(.width(32), .enable("false")) multiplexer_1 (.in0(m1_0_A2), .in1(m1_0), .out(m1), .sel(m1_positiva));
  Complemento_A2 complemento_a2_1 (.Num(m1_0), .Num_A2(m1_0_A2));
  Register #(.width(32)) u_X1 (.D(Input), .en(L0), .Q(X1), .clk(CLk), .clr(Clear));
  // Probe on m1_0
  // Probe on m1_1
  // Probe on m1
  Subtractor #(.width(32)) subtractor_1 (.a(Y1), .b(Y2), .out(resta1));  // open: bin, bout
  // Probe on resta1
  Subtractor #(.width(32)) subtractor_2 (.a(X1), .b(X2), .out(resta2));  // open: bin, bout
  // Probe on resta2
  and and_1 (resta2_negativa, resta2[31], 1'b1);
  Register #(.width(32)) u_Y1 (.D(Input), .en(L1), .Q(Y1), .clk(CLk), .clr(Clear));
  or or_1 (C, C1, C2, C3, V_H);
  and and_2 (resta1_negativa, resta1[31], 1'b1);
  // Probe on m2_0
  Divider #(.width(32)) divider_2 (.a(r3), .b(r4), .out(m2_0), .rem(m2_1));  // open: upper
  // Probe on m2_1
  Multiplexer #(.width(32), .enable("false")) multiplexer_2 (.in0(m2_0_A2), .in1(m2_0), .out(m2), .sel(m2_positiva));
  // Probe on m2
  Register #(.width(32)) u_X2 (.D(Input), .en(L2), .Q(X2), .clk(CLk), .clr(Clear));
  Register #(.width(32)) u_Y2 (.D(Input), .en(L3), .Q(Y2), .clk(CLk), .clr(Clear));
  // Probe on r1
  Multiplexer #(.width(32), .enable("false")) multiplexer_3 (
    .in0(resta1), .in1(resta1_A2), .out(r1), .sel(resta1_negativa));
  Register #(.width(32)) u_X3 (.D(Input), .en(L4), .Q(X3), .clk(CLk), .clr(Clear));
  // Probe on m3_0
  Divider #(.width(32)) divider_3 (.a(r5), .b(r6), .out(m3_0), .rem(m3_1));  // open: upper
  // Probe on m3_1
  Multiplexer #(.width(32), .enable("false")) multiplexer_4 (.in0(m3_0_A2), .in1(m3_0), .out(m3), .sel(m3_positiva));
  Multiplexer #(.width(7)) multiplexer_5 (.in0(7'b1000110), .in1(7'b1010100), .out(Output), .sel(C), .en(END));
  Multiplexer #(.width(32), .enable("false")) multiplexer_6 (
    .in0(resta2), .in1(resta2_A2), .out(r2), .sel(resta2_negativa));
  // Probe on m3
  // Probe on r2
  Register #(.width(32)) u_Y3 (.D(Input), .en(L5), .Q(Y3), .clk(CLk), .clr(Clear));
  Complemento_A2 complemento_a2_2 (.Num(resta1), .Num_A2(resta1_A2));
  Complemento_A2 complemento_a2_3 (.Num(resta2), .Num_A2(resta2_A2));
  // Probe on r1_0
  Register #(.width(32)) u_r1 (.D(m1), .en(L6), .Q(r1_0), .clk(CLk), .clr(Clear));
  Complemento_A2 complemento_a2_4 (.Num(m2_0), .Num_A2(m2_0_A2));
  Complemento_A2 complemento_a2_5 (.Num(m3_0), .Num_A2(m3_0_A2));
  Adder #(.width(24)) adder_1 (.a(Adress), .b(24'h1), .out(w___1));  // open: cin, cout
  xnor xnor_1 (m1_positiva, resta1_negativa, resta2_negativa);
  Register #(.width(32)) u_r2 (.D(m2), .en(L6), .Q(r2_0), .clk(CLk), .clr(Clear));
  // Probe on r2_0
  // Probe on resta1_A2
  // Probe on resta2_A2
  // Probe on r3_0
  Register #(.width(32)) u_r3 (.D(m3), .en(L6), .Q(r3_0), .clk(CLk), .clr(Clear));
  Multiplexer #(.width(24), .enable("false")) multiplexer_7 (
    .in0({24{1'b0}}), .in1(w___1), .out(multiplexer_7_out), .sel(Sw));
  // Probe on multiplier_1_out
  Multiplier #(.width(32)) multiplier_1 (.a(r1_0), .b(r2_0), .out(multiplier_1_out));  // open: cin, cout
  Multiplier #(.width(32)) multiplier_2 (.a(r2_0), .b(r3_0), .out(multiplier_2_out));  // open: cin, cout
  Multiplier #(.width(32)) multiplier_3 (.a(r3_0), .b(r1_0), .out(multiplier_3_out));  // open: cin, cout
  // Probe on {32{1'b1}}
  Comparator #(.width(32)) comparator_1 (.a(multiplier_1_out), .b({32{1'b1}}), .eq(C1));  // open: gt, lt
  Comparator #(.width(32)) comparator_2 (.a(multiplier_2_out), .b({32{1'b1}}), .eq(C2));  // open: gt, lt
  Comparator #(.width(32)) comparator_3 (.a(multiplier_3_out), .b({32{1'b1}}), .eq(C3));  // open: gt, lt
  // Probe on m1
  // Probe on {32{1'b0}}
  Register #(.width(24)) u_Adress (.D(multiplexer_7_out), .en(Lw), .Q(Adress), .clk(CLk), .clr(Clear));
  Comparator #(.width(32)) comparator_4 (.a(m1), .b({32{1'b0}}), .eq(T1));  // open: gt, lt
  Comparator #(.width(32)) comparator_5 (.a(m2), .b({32{1'b0}}), .eq(T2));  // open: gt, lt
  Comparator #(.width(32)) comparator_6 (.a(m3), .b({32{1'b0}}), .eq(T3));  // open: gt, lt
  Multiplexer #(.width(32), .enable("false")) multiplexer_8 (
    .in0(resta3), .in1(resta3_A2), .out(r3), .sel(resta3_negativa));
  // Probe on r5
  Multiplexer #(.width(32), .enable("false")) multiplexer_9 (
    .in0(resta5), .in1(resta5_A2), .out(r5), .sel(resta5_negativa));
  not not_1 (not_1_out, V1);
  not not_2 (not_2_out, V2);
  not not_3 (not_3_out, V3);
  // Probe on r3
  Subtractor #(.width(32)) subtractor_3 (.a(Y2), .b(Y3), .out(resta3));  // open: bin, bout
  // Probe on resta3
  Subtractor #(.width(32)) subtractor_4 (.a(X2), .b(X3), .out(resta4));  // open: bin, bout
  // Probe on resta4
  Subtractor #(.width(32)) subtractor_5 (.a(Y3), .b(Y1), .out(resta5));  // open: bin, bout
  // Probe on resta5
  Subtractor #(.width(32)) subtractor_6 (.a(X3), .b(X1), .out(resta6));  // open: bin, bout
  // Probe on resta6
  and and_3 (H1, T1, not_1_out);
  and and_4 (H2, T2, not_2_out);
  and and_5 (H3, T3, not_3_out);
  and and_6 (resta4_negativa, resta4[31], 1'b1);
  Multiplexer #(.width(32), .enable("false")) multiplexer_10 (
    .in0(resta6), .in1(resta6_A2), .out(r6), .sel(resta6_negativa));
  and and_7 (resta5_negativa, resta5[31], 1'b1);
  and and_8 (resta6_negativa, resta6[31], 1'b1);
  // Probe on r4
  Multiplexer #(.width(32), .enable("false")) multiplexer_11 (
    .in0(resta4), .in1(resta4_A2), .out(r4), .sel(resta4_negativa));
  and and_9 (resta3_negativa, resta3[31], 1'b1);
  // Probe on r6
  Complemento_A2 complemento_a2_6 (.Num(resta3), .Num_A2(resta3_A2));
  Complemento_A2 complemento_a2_7 (.Num(resta4), .Num_A2(resta4_A2));
  Complemento_A2 complemento_a2_8 (.Num(resta5), .Num_A2(resta5_A2));
  Complemento_A2 complemento_a2_9 (.Num(resta6), .Num_A2(resta6_A2));
  xnor xnor_2 (m2_positiva, resta3_negativa, resta4_negativa);
  // Probe on resta3_A2
  // Probe on resta4_A2
  or or_2 (or_2_out, V1, V2, V3);
  or or_3 (or_3_out, H1, H2, H3);
  xnor xnor_3 (m3_positiva, resta5_negativa, resta6_negativa);
  // Probe on resta5_A2
  // Probe on resta6_A2
  and and_10 (V_H, or_2_out, or_3_out);
  // Probe on resta2
  // Probe on {32{1'b0}}
  Comparator #(.width(32)) comparator_7 (.a(resta2), .b({32{1'b0}}), .eq(V1));  // open: gt, lt
  Comparator #(.width(32)) comparator_8 (.a(resta4), .b({32{1'b0}}), .eq(V2));  // open: gt, lt
  Comparator #(.width(32)) comparator_9 (.a(resta6), .b({32{1'b0}}), .eq(V3));  // open: gt, lt

  // Other names for the same wires on the sheet: clock = CLk; w[23:0] = Adress; w0[31:0] = Input
endmodule

module Rectangulo_CU (
  input  Start,
  input  CLR,
  input  Print_End,
  input  C,
  input  CLK,
  output END,
  output Lw,
  output L0,
  output L1,
  output L2,
  output L3,
  output L4,
  output L5,
  output L6,
  output Sw,
  output Start_Print
);

  wire demultiplexer_1_out0, demultiplexer_2_out0, demultiplexer_2_out1, demultiplexer_3_out0,
       demultiplexer_3_out1, demultiplexer_4_out0, demultiplexer_4_out1, IDLE_q, or_1_out, or_5_out,
       or_6_out, Print_q, T_q, WAIT_7_q;

  or or_1 (or_1_out, demultiplexer_1_out0, demultiplexer_3_out1);
  D_Flip_Flop IDLE (.clk(CLK), .D(or_1_out), .Q(IDLE_q), .preset(Start));  // open: Qn, en, reset
  Demultiplexer #(.enable("false")) demultiplexer_1 (.out0(demultiplexer_1_out0), .out1(L0), .in(IDLE_q), .sel(Start));
  or or_2 (Lw, L0, L1, L2, L3, L4, L5);
  D_Flip_Flop WAIT (.clk(CLK), .D(L0), .Q(L1));  // open: Qn, preset, en, reset
  D_Flip_Flop WAIT_2 (.clk(CLK), .D(L1), .Q(L2));  // open: Qn, preset, en, reset
  D_Flip_Flop WAIT_3 (.clk(CLK), .D(L2), .Q(L3));  // open: Qn, preset, en, reset
  D_Flip_Flop WAIT_4 (.clk(CLK), .D(L3), .Q(L4));  // open: Qn, preset, en, reset
  or or_3 (Sw, L1, L2, L3, L4, L5);
  D_Flip_Flop WAIT_5 (.clk(CLK), .D(L4), .Q(L5));  // open: Qn, preset, en, reset
  Demultiplexer #(.enable("false")) demultiplexer_2 (
    .out0(demultiplexer_2_out0), .out1(demultiplexer_2_out1), .in(WAIT_7_q), .sel(C));
  D_Flip_Flop WAIT_6 (.clk(CLK), .D(L5), .Q(L6));  // open: Qn, preset, en, reset
  D_Flip_Flop WAIT_7 (.clk(CLK), .D(L6), .Q(WAIT_7_q));  // open: Qn, preset, en, reset
  D_Flip_Flop T (.clk(CLK), .D(demultiplexer_2_out1), .Q(T_q));  // open: Qn, preset, en, reset
  or or_4 (Start_Print, demultiplexer_2_out0, T_q);
  or or_5 (or_5_out, demultiplexer_3_out0, demultiplexer_4_out1);
  or or_6 (or_6_out, demultiplexer_4_out0, Start_Print);
  D_Flip_Flop u_END (.clk(CLK), .D(or_5_out), .Q(END));  // open: Qn, preset, en, reset
  D_Flip_Flop Print (.clk(CLK), .D(or_6_out), .Q(Print_q), .reset(CLR));  // open: Qn, preset, en
  Demultiplexer #(.enable("false")) demultiplexer_3 (
    .out0(demultiplexer_3_out0), .out1(demultiplexer_3_out1), .in(END), .sel(Start));
  Demultiplexer #(.enable("false")) demultiplexer_4 (
    .out0(demultiplexer_4_out0), .out1(demultiplexer_4_out1), .in(Print_q), .sel(Print_End));

  // Other names for the same wires on the sheet: Clear = CLR; clock = CLK; Lw0 = L0; Lw1 = L1; Sw1 = L1; Lw2 = L2;
  //   Sw2 = L2; Lw3 = L3; Sw3 = L3; Lw4 = L4; Sw4 = L4; Lw5 = L5; Sw5 = L5
endmodule

module Media_DP (
  input  END,
  input  CLR,
  input  CLk,
  input  Ln,
  input  Ls0,
  input  Ls1,
  input  Ls2,
  input  Li0,
  input  Li1,
  input  Lw,
  input  Sw,
  input  Si,
  input  Ss0,
  input  Ss1,
  input  [31:0] Input,
  output [31:0] Output,
  output [23:0] Adress,
  output i____n
);

  wire comparator_1_eq, comparator_1_lt, or_1_out, or_2_out, Sum_negative;
  wire [23:0] multiplexer_6_out, w___1;
  wire [31:0] i, i___1, multiplexer_1_out, multiplexer_3_out, N, Sum, Sum0, Sum___w_i, Sum_A2, Sum_n,
       Sum_n_0, Sum_n_0__A2;

  Register #(.width(32)) u_N (.D(Input), .en(Ln), .Q(N), .clk(CLk), .clr(CLR));
  Adder #(.width(24)) adder_1 (.a(Adress), .b(24'h1), .out(w___1));  // open: cin, cout
  Adder #(.width(32)) adder_2 (.a(i), .b(32'h1), .out(i___1));  // open: cin, cout
  Complemento_A2 complemento_a2_1 (.Num(Sum), .Num_A2(Sum_A2));
  Multiplexer #(.width(32), .enable("false")) multiplexer_1 (
    .in1(Sum___w_i), .out(multiplexer_1_out), .sel(Ss0));  // open: in0
  // Probe on Sum
  Register #(.width(32)) u_Sum (.D(multiplexer_1_out), .en(or_1_out), .Q(Sum), .clk(CLk), .clr(CLR));
  or or_1 (or_1_out, Ls0, Ls2, Ls1);
  Adder #(.width(32)) adder_3 (.a(Sum), .b(Input), .out(Sum___w_i));  // open: cin, cout
  and and_1 (Sum_negative, Sum[31], 1'b1);
  Multiplexer #(.width(32)) multiplexer_2 (.in0({32{1'b0}}), .in1(Sum_n), .out(Output), .sel(END), .en(END));
  Multiplexer #(.width(32), .enable("false")) multiplexer_3 (
    .in0(32'h1), .in1(i___1), .out(multiplexer_3_out), .sel(Si));
  // Probe on Output
  Register #(.width(32)) u_I (.D(multiplexer_3_out), .en(or_2_out), .Q(i), .clk(CLk), .clr(CLR));
  or or_2 (or_2_out, Li0, Li1);
  Divider #(.width(32)) divider_1 (.a(Sum0), .b(N), .out(Sum_n_0));  // open: upper, rem
  Multiplexer #(.width(32), .enable("false")) multiplexer_4 (
    .in0(Sum_n_0), .in1(Sum_n_0__A2), .out(Sum_n), .sel(Sum_negative));
  // Probe on Sum0
  Multiplexer #(.width(32), .enable("false")) multiplexer_5 (.in0(Sum), .in1(Sum_A2), .out(Sum0), .sel(Sum_negative));
  Comparator #(.width(32)) comparator_1 (.a(i), .b(N), .eq(comparator_1_eq), .lt(comparator_1_lt));  // open: gt
  Multiplexer #(.width(24), .enable("false")) multiplexer_6 (
    .in0({24{1'b0}}), .in1(w___1), .out(multiplexer_6_out), .sel(Sw));
  or or_3 (i____n, comparator_1_eq, comparator_1_lt);
  Complemento_A2 complemento_a2_2 (.Num(Sum_n_0), .Num_A2(Sum_n_0__A2));
  Register #(.width(24)) u_Adress (.D(multiplexer_6_out), .en(Lw), .Q(Adress), .clk(CLk), .clr(CLR));

  // Other names for the same wires on the sheet: Clear = CLR; clock = CLk; w[23:0] = Adress; w0[31:0] = Input
endmodule

module Media_CU (
  input  Start,
  input  CLR,
  input  i____n,
  input  CLK,
  output END,
  output Ln,
  output Ls0,
  output Li0,
  output Li1,
  output Ls1,
  output Ss0,
  output Si,
  output Ss1,
  output Ls2,
  output Sw,
  output Lw
);

  wire demultiplexer_1_out0, demultiplexer_3_out0, demultiplexer_3_out1, IDLE_q, or_1_out, or_3_out,
       or_5_out, WHILE_q;

  or or_1 (or_1_out, demultiplexer_1_out0, demultiplexer_3_out1);
  D_Flip_Flop IDLE (.clk(CLK), .D(or_1_out), .Q(IDLE_q), .preset(Start));  // open: Qn, en, reset
  Demultiplexer #(.enable("false")) demultiplexer_1 (.out0(demultiplexer_1_out0), .out1(Li0), .in(IDLE_q), .sel(Start));
  or or_2 (Lw, Li0, Li1);
  or or_3 (or_3_out, Li0, Li1);
  D_Flip_Flop WHILE (.clk(CLK), .D(or_3_out), .Q(WHILE_q), .reset(CLR));  // open: Qn, preset, en
  Demultiplexer #(.enable("false")) demultiplexer_2 (.out0(Ls2), .out1(Li1), .in(WHILE_q), .sel(i____n));
  or or_4 (Sw, Li0, Li1);
  or or_5 (or_5_out, demultiplexer_3_out0, Ls2);
  D_Flip_Flop u_END (.clk(CLK), .D(or_5_out), .Q(END), .reset(CLR));  // open: Qn, preset, en
  Demultiplexer #(.enable("false")) demultiplexer_3 (
    .out0(demultiplexer_3_out0), .out1(demultiplexer_3_out1), .in(END), .sel(Start));

  assign Ln = Li0;
  assign Ls0 = Li0;
  assign Ls1 = Li1;
  assign Si = Li1;
  assign Ss0 = Li1;
  assign Ss1 = Ls2;

  // Other names for the same wires on the sheet: Clear = CLR; clock = CLK; Lw0 = Li0; Sw0 = Li0; Lw1 = Li1; Sw1 = Li1
endmodule

module Varianza_DP (
  input  END,
  input  CLR,
  input  CLk,
  input  Ln,
  input  Ls0,
  input  Ls1,
  input  Ls2,
  input  Li0,
  input  Li1,
  input  Lw,
  input  Sw,
  input  Si,
  input  Ss0,
  input  Ss1,
  input  Lm,
  input  [31:0] media,
  input  [31:0] Input,
  output [31:0] Output,
  output i____n,
  output [23:0] Adress
);

  wire comparator_1_eq, comparator_1_lt, or_1_out, or_2_out, Sum_negative, V1;
  wire [23:0] multiplexer_6_out, w___1;
  wire [31:0] divider_1_out, i, i___1, Media_t, multiplexer_2_out, multiplexer_3_out, N, N_1,
       subtractor_2_out, Sum, Sum0, Sum___w_i, Sum__N___1__0, Sum__N___1__0__A2, Sum_A2, w_i____Media_2;

  Register #(.width(32)) u_N (.D(Input), .en(Ln), .Q(N), .clk(CLk), .clr(CLR));
  Adder #(.width(24)) adder_1 (.a(Adress), .b(24'h1), .out(w___1));  // open: cin, cout
  Adder #(.width(32)) adder_2 (.a(i), .b(32'h1), .out(i___1));  // open: cin, cout
  Adder #(.width(32)) adder_3 (.a(Sum), .b(w_i____Media_2), .out(Sum___w_i));  // open: cin, cout
  Complemento_A2 complemento_a2_1 (.Num(Sum), .Num_A2(Sum_A2));
  Multiplexer #(.width(32), .enable("false")) multiplexer_1 (
    .in0(Sum__N___1__0), .in1(Sum__N___1__0__A2), .out(Output), .sel(Sum_negative));
  Multiplexer #(.width(32), .enable("false")) multiplexer_2 (
    .in1(Sum___w_i), .out(multiplexer_2_out), .sel(Ss0));  // open: in0
  // Probe on Output
  // Probe on Sum
  Register #(.width(32)) u_Sum (.D(multiplexer_2_out), .en(or_1_out), .Q(Sum), .clk(CLk), .clr(CLR));
  or or_1 (or_1_out, Ls0, Ls2, Ls1);
  Subtractor #(.width(32)) subtractor_1 (.a(N), .b(32'h1), .out(N_1));  // open: bin, bout
  // Probe on N_1
  Subtractor #(.width(32)) subtractor_2 (.a(Input), .b(Media_t), .out(subtractor_2_out));  // open: bin, bout
  and and_1 (Sum_negative, Sum[31], 1'b1);
  // Probe on Output
  Divider #(.width(32)) divider_1 (.a(Sum0), .b(N_1), .out(divider_1_out));  // open: upper, rem
  Multiplier #(.width(32)) multiplier_1 (
    .a(subtractor_2_out), .b(subtractor_2_out), .out(w_i____Media_2));  // open: cin, cout
  Multiplexer #(.width(32), .enable("false")) multiplexer_3 (
    .in0(32'h1), .in1(i___1), .out(multiplexer_3_out), .sel(Si));
  Multiplexer #(.width(32), .enable("false")) multiplexer_4 (
    .in0(divider_1_out), .in1({32{1'b0}}), .out(Sum__N___1__0), .sel(V1));
  // Probe on w_i____Media_2
  Register #(.width(32)) u_I (.D(multiplexer_3_out), .en(or_2_out), .Q(i), .clk(CLk), .clr(CLR));
  or or_2 (or_2_out, Li0, Li1);
  // Probe on Sum__N___1__0
  // Probe on Output
  // Probe on Sum0
  Multiplexer #(.width(32), .enable("false")) multiplexer_5 (.in0(Sum), .in1(Sum_A2), .out(Sum0), .sel(Sum_negative));
  Register #(.width(32)) u_Media (.D(media), .en(Lm), .Q(Media_t), .clk(CLk), .clr(CLR));
  Comparator #(.width(32)) comparator_1 (.a(i), .b(N), .eq(comparator_1_eq), .lt(comparator_1_lt));  // open: gt
  Multiplexer #(.width(24), .enable("false")) multiplexer_6 (
    .in0({24{1'b0}}), .in1(w___1), .out(multiplexer_6_out), .sel(Sw));
  or or_3 (i____n, comparator_1_eq, comparator_1_lt);
  Complemento_A2 complemento_a2_2 (.Num(Sum__N___1__0), .Num_A2(Sum__N___1__0__A2));
  // Probe on N_1
  Register #(.width(24)) u_Adress (.D(multiplexer_6_out), .en(Lw), .Q(Adress), .clk(CLk), .clr(CLR));
  Comparator #(.width(32)) comparator_2 (.a(N_1), .b({32{1'b0}}), .eq(V1));  // open: gt, lt

  // Other names for the same wires on the sheet: Clear = CLR; clock = CLk; Final[31:0] = Output;
  //   Sum__N___1[31:0] = Output; w[23:0] = Adress; w0[31:0] = Input
endmodule

module Varianza_CU (
  input  Start,
  input  CLR,
  input  Print_End,
  input  i____n,
  input  CLK,
  input  Media_End,
  output END,
  output Ln,
  output Ls0,
  output Li0,
  output Li1,
  output Ls1,
  output Ss0,
  output Si,
  output Ss1,
  output Ls2,
  output Sw,
  output Lw,
  output Lm,
  output Start_Print
);

  wire demultiplexer_1_out0, demultiplexer_3_out0, demultiplexer_3_out1, demultiplexer_4_out0,
       demultiplexer_4_out1, IDLE_q, or_1_out, or_3_out, or_5_out, or_6_out, Print_q, WHILE_q;

  or or_1 (or_1_out, demultiplexer_1_out0, demultiplexer_3_out1);
  D_Flip_Flop IDLE (.clk(CLK), .D(or_1_out), .Q(IDLE_q), .preset(Start));  // open: Qn, en, reset
  Demultiplexer #(.enable("false")) demultiplexer_1 (
    .out0(demultiplexer_1_out0), .out1(Li0), .in(IDLE_q), .sel(Media_End));
  or or_2 (Lw, Li0, Li1);
  or or_3 (or_3_out, Li0, Li1);
  D_Flip_Flop WHILE (.clk(CLK), .D(or_3_out), .Q(WHILE_q), .reset(CLR));  // open: Qn, preset, en
  Demultiplexer #(.enable("false")) demultiplexer_2 (.out0(Ls2), .out1(Li1), .in(WHILE_q), .sel(i____n));
  or or_4 (Sw, Li0, Li1);
  or or_5 (or_5_out, demultiplexer_3_out0, demultiplexer_4_out1);
  D_Flip_Flop u_END (.clk(CLK), .D(or_5_out), .Q(END), .reset(CLR));  // open: Qn, preset, en
  Demultiplexer #(.enable("false")) demultiplexer_3 (
    .out0(demultiplexer_3_out0), .out1(demultiplexer_3_out1), .in(END), .sel(Start));
  D_Flip_Flop WAIT (.clk(CLK), .D(Ls2), .Q(Start_Print), .reset(CLR));  // open: Qn, preset, en
  or or_6 (or_6_out, demultiplexer_4_out0, Start_Print);
  and and_1 (Lm, Li0, Media_End);
  D_Flip_Flop Print (.clk(CLK), .D(or_6_out), .Q(Print_q), .reset(CLR));  // open: Qn, preset, en
  Demultiplexer #(.enable("false")) demultiplexer_4 (
    .out0(demultiplexer_4_out0), .out1(demultiplexer_4_out1), .in(Print_q), .sel(Print_End));

  assign Ln = Li0;
  assign Ls0 = Li0;
  assign Ls1 = Li1;
  assign Si = Li1;
  assign Ss0 = Li1;
  assign Ss1 = Ls2;

  // Other names for the same wires on the sheet: Clear = CLR; clock = CLK; Lm_t = Li0; Lw0 = Li0; Sw0 = Li0;
  //   Lw1 = Li1; Sw1 = Li1
endmodule

module BIG_ASM_CUBO (
  input  [31:0] DATA_INPUT,
  input  [31:0] MEMORY_IN,
  input  CLK,
  input  CLR,
  input  start,
  output [23:0] DIR_INPUT,
  output [31:0] MEMORY_OUT,
  output [23:0] DIR_MEMORY,
  output Write_OUTPUT,
  output [6:0] ASCII,
  output Write_ASCII,
  output END
);

  wire cubo_cu_1_start_print, Lx0, Lx1, print_dec_1_end, Sx;
  wire [31:0] cubo_dp_1_output;

  Cubo_DP cubo_dp_1 (
    .Addres(DIR_INPUT), .Input(DATA_INPUT), .CLk(CLK), .Output(cubo_dp_1_output), .Lx0(Lx0), .Lx1(Lx1),
    .Sx(Sx), .CLR(CLR));
  Cubo_CU cubo_cu_1 (
    .CLK(CLK), .Start(start), .Lx0(Lx0), .Sx(Sx), .Lx1(Lx1), .END(END), .Print_End(print_dec_1_end),
    .Start_Print(cubo_cu_1_start_print), .CLR(CLR));
  // Probe on cubo_dp_1_output
  PRINT_DEC print_dec_1 (
    .num(cubo_dp_1_output), .start(cubo_cu_1_start_print), .CLK(CLK), .RST(CLR), .ASCII(ASCII),
    .Write_ASCII(Write_ASCII), .END(print_dec_1_end));

  // Other names for the same wires on the sheet: clock = CLK
endmodule

module BIG_ASM_PARALELAS (
  input  [31:0] DATA_INPUT,
  input  [31:0] MEMORY_IN,
  input  CLK,
  input  CLR,
  input  start,
  output [23:0] DIR_INPUT,
  output [31:0] MEMORY_OUT,
  output [23:0] DIR_MEMORY,
  output Write_OUTPUT,
  output [6:0] ASCII,
  output Write_ASCII,
  output END
);

  wire L0, L1, L2, L3, L4, L5, L6, L7, Lw, paralelas_dp_1_p, Sw, WAIT_q;

  Paralelas_DP paralelas_dp_1 (
    .Adress(DIR_INPUT), .CLk_2(CLK), .Input(DATA_INPUT), .END(Write_ASCII), .Output(ASCII), .L0(L0), .L1(L1),
    .L2(L2), .L3(L3), .L4(L4), .L5(L5), .L6(L6), .L7(L7), .Lw(Lw), .Sw(Sw), .P(paralelas_dp_1_p), .CLk(CLR));
  Paralelas_CU paralelas_cu_1 (
    .END(END), .CLK(CLK), .Start(start), .P(paralelas_dp_1_p), .L0(L0), .L1(L1), .L2(L2), .L3(L3), .L4(L4),
    .L5(L5), .L6(L6), .L7(L7), .Sw(Sw), .Lw(Lw), .Print_End(WAIT_q), .Start_Print(Write_ASCII), .CLR(CLR));
  D_Flip_Flop WAIT (.clk(CLK), .D(Write_ASCII), .Q(WAIT_q));  // open: Qn, preset, en, reset
  // Probe on Write_ASCII

  // Other names for the same wires on the sheet: clear = CLR; clock = CLK
endmodule

module BIG_ASM_RECTANGULO (
  input  [31:0] DATA_INPUT,
  input  [31:0] MEMORY_IN,
  input  CLK,
  input  CLR,
  input  start,
  output [23:0] DIR_INPUT,
  output [31:0] MEMORY_OUT,
  output [23:0] DIR_MEMORY,
  output Write_OUTPUT,
  output [6:0] ASCII,
  output Write_ASCII,
  output END
);

  wire L0, L1, L2, L3, L4, L5, L6, Lw, rectangulo_dp_1_c, Sw, WAIT_q;

  Rectangulo_DP rectangulo_dp_1 (
    .Adress(DIR_INPUT), .CLk(CLK), .Input(DATA_INPUT), .END(Write_ASCII), .C(rectangulo_dp_1_c),
    .Output(ASCII), .L0(L0), .L1(L1), .L2(L2), .L3(L3), .L4(L4), .L5(L5), .L6(L6), .Lw(Lw), .Sw(Sw),
    .Clear(CLR));
  Rectangulo_CU rectangulo_cu_1 (
    .END(END), .CLK(CLK), .Start(start), .C(rectangulo_dp_1_c), .Lw(Lw), .L0(L0), .L1(L1), .L2(L2), .L3(L3),
    .L4(L4), .L5(L5), .L6(L6), .Sw(Sw), .CLR(CLR), .Print_End(WAIT_q), .Start_Print(Write_ASCII));
  D_Flip_Flop WAIT (.clk(CLK), .D(Write_ASCII), .Q(WAIT_q));  // open: Qn, preset, en, reset
  // Probe on Write_ASCII

  // Other names for the same wires on the sheet: clear = CLR; clock = CLK
endmodule

module BIG_ASM_VARIANZA (
  input  [31:0] DATA_INPUT,
  input  [31:0] MEMORY_IN,
  input  CLK,
  input  CLR,
  input  start,
  output [23:0] DIR_INPUT,
  output [31:0] MEMORY_OUT,
  output [23:0] DIR_MEMORY,
  output Write_OUTPUT,
  output [6:0] ASCII,
  output Write_ASCII,
  output END
);

  wire i____n, Li0, Li0_2, Li1, Li1_2, Lm, Ln, Ln_2, Ls0, Ls0_2, Ls1, Ls1_2, Ls2, Ls2_2, Lw, Lw_2,
       media_dp_1_i____n, Media_End, print_dec_1_end, Si, Si_2, Ss0, Ss0_2, Ss1, Ss1_2, Sw, Sw_2,
       varianza_cu_1_start_print;
  wire [23:0] adress_V, media_dp_1_adress;
  wire [31:0] Media, varianza_dp_1_output;

  Media_DP media_dp_1 (
    .END(Media_End), .Adress(media_dp_1_adress), .CLk(CLK), .Input(DATA_INPUT), .Output(Media), .Ln(Ln),
    .Ls0(Ls0), .Ls1(Ls1), .Ls2(Ls2), .Li0(Li0), .Li1(Li1), .Lw(Lw), .Sw(Sw), .Si(Si), .Ss0(Ss0), .Ss1(Ss1),
    .CLR(CLR), .i____n(media_dp_1_i____n));
  Varianza_DP varianza_dp_1 (
    .END(varianza_cu_1_start_print), .Adress(adress_V), .CLk(CLK), .Input(DATA_INPUT),
    .Output(varianza_dp_1_output), .Ln(Ln_2), .Ls0(Ls0_2), .Ls1(Ls1_2), .Ls2(Ls2_2), .Li0(Li0_2),
    .Li1(Li1_2), .Lw(Lw_2), .Sw(Sw_2), .Si(Si_2), .Ss0(Ss0_2), .Ss1(Ss1_2), .Lm(Lm), .media(Media),
    .CLR(CLR), .i____n(i____n));
  Media_CU media_cu_1 (
    .CLK(CLK), .Start(start), .Ln(Ln), .Ls0(Ls0), .Li0(Li0), .Li1(Li1), .Ls1(Ls1), .Ss0(Ss0), .Si(Si),
    .i____n(media_dp_1_i____n), .Ss1(Ss1), .Ls2(Ls2), .Sw(Sw), .Lw(Lw), .CLR(CLR), .END(Media_End));
  Varianza_CU varianza_cu_1 (
    .CLK(CLK), .Start(start), .Ln(Ln_2), .Ls0(Ls0_2), .Li0(Li0_2), .Li1(Li1_2), .Ls1(Ls1_2), .Ss0(Ss0_2),
    .Si(Si_2), .i____n(i____n), .Ss1(Ss1_2), .Ls2(Ls2_2), .Sw(Sw_2), .Lw(Lw_2), .Lm(Lm),
    .Media_End(Media_End), .CLR(CLR), .Start_Print(varianza_cu_1_start_print), .Print_End(print_dec_1_end),
    .END(END));
  PRINT_DEC print_dec_1 (
    .num(varianza_dp_1_output), .start(varianza_cu_1_start_print), .CLK(CLK), .RST(CLR), .ASCII(ASCII),
    .Write_ASCII(Write_ASCII), .END(print_dec_1_end));
  Multiplexer #(.width(24), .enable("false")) multiplexer_1 (
    .in0(media_dp_1_adress), .in1(adress_V), .out(DIR_INPUT), .sel(Media_End));

  // Other names for the same wires on the sheet: clear = CLR; clock = CLK
endmodule

module Complemento_A2 (
  input  [31:0] Num,
  output [31:0] Num_A2
);

  wire [31:0] Invertido;

  not not_1 (Invertido[30], Num[30]);
  not not_2 (Invertido[31], Num[31]);
  not not_3 (Invertido[29], Num[29]);
  not not_4 (Invertido[28], Num[28]);
  not not_5 (Invertido[27], Num[27]);
  not not_6 (Invertido[25], Num[25]);
  not not_7 (Invertido[26], Num[26]);
  not not_8 (Invertido[24], Num[24]);
  not not_9 (Invertido[22], Num[22]);
  not not_10 (Invertido[23], Num[23]);
  not not_11 (Invertido[21], Num[21]);
  not not_12 (Invertido[19], Num[19]);
  not not_13 (Invertido[20], Num[20]);
  not not_14 (Invertido[18], Num[18]);
  not not_15 (Invertido[17], Num[17]);
  not not_16 (Invertido[13], Num[13]);
  not not_17 (Invertido[16], Num[16]);
  not not_18 (Invertido[15], Num[15]);
  not not_19 (Invertido[14], Num[14]);
  not not_20 (Invertido[9], Num[9]);
  not not_21 (Invertido[11], Num[11]);
  not not_22 (Invertido[12], Num[12]);
  not not_23 (Invertido[10], Num[10]);
  // Probe on Invertido
  not not_24 (Invertido[8], Num[8]);
  not not_25 (Invertido[7], Num[7]);
  not not_26 (Invertido[5], Num[5]);
  not not_27 (Invertido[6], Num[6]);
  not not_28 (Invertido[2], Num[2]);
  not not_29 (Invertido[4], Num[4]);
  not not_30 (Invertido[1], Num[1]);
  not not_31 (Invertido[3], Num[3]);
  not not_32 (Invertido[0], Num[0]);
  Adder #(.width(32)) adder_1 (.a(Invertido), .b(32'h1), .out(Num_A2));  // open: cin, cout
endmodule
